// Logisim project stack_logical_normal.circ as structural Verilog: 25 circuits, main circuit main
module main (
  input  CLK,
  input  RESET,
  input  [1:0] COMMAND,
  input  [2:0] INDEX,
  input  [3:0] IO_DATA_in,
  output [3:0] IO_DATA_out
);

  wire [3:0] stack_1_d0, stack_1_d1, stack_1_d2, stack_1_d3, stack_1_d4;

  // Probe on stack_1_d0
  stack stack_1 (
    .CLK(CLK), .RESET(RESET), .COMMAND(COMMAND), .INDEX(INDEX), .IO_DATA_in(IO_DATA_in), .d0(stack_1_d0),
    .d1(stack_1_d1), .d2(stack_1_d2), .d3(stack_1_d3), .d4(stack_1_d4), .IO_DATA_out(IO_DATA_out));
  // Probe on stack_1_d1
  // Probe on stack_1_d2
  // Probe on stack_1_d3
  // Probe on stack_1_d4
endmodule

module stack (
  input  CLK,
  input  RESET,
  input  [1:0] COMMAND,
  input  [2:0] INDEX,
  input  [3:0] IO_DATA_in,
  output [3:0] d0,
  output [3:0] d1,
  output [3:0] d2,
  output [3:0] d3,
  output [3:0] d4,
  output [3:0] IO_DATA_out
);

  wire and_5_out, GET, not_1_out, not_2_out, not_3_out, not_4_out, not_5_out, not_6_out, or_1_out, POP, PUSH,
       ZERO;
  wire [3:0] stack_interface_1_out_data, transmission_1_p4;

  not not_1 (not_1_out, COMMAND[1]);
  not not_2 (not_2_out, COMMAND[0]);
  not not_3 (not_3_out, COMMAND[0]);
  not not_4 (not_4_out, COMMAND[1]);
  and and_1 (PUSH, COMMAND[0], not_1_out);
  and and_2 (POP, not_2_out, COMMAND[1]);
  and and_3 (GET, COMMAND[0], COMMAND[1]);
  and and_4 (ZERO, not_3_out, not_4_out);
  stack_interface stack_interface_1 (
    .CLK(CLK), .RESET(RESET), .COMMAND(COMMAND), .INDEX(INDEX), .IN_DATA(transmission_1_p4), .d0(d0),
    .d1(d1), .d2(d2), .d3(d3), .d4(d4), .OUT_DATA(stack_interface_1_out_data));
  not not_5 (not_5_out, PUSH);
  // Transmission_Gate #(.width(4)) transmission_1: pin names not known; wires that end beside it: IO_DATA_in, not_5_out, PUSH, transmission_1_p4
  not not_6 (not_6_out, and_5_out);
  or or_1 (or_1_out, POP, GET);
  and and_5 (and_5_out, or_1_out, CLK);
  // Transmission_Gate #(.width(4)) transmission_2: pin names not known; wires that end beside it: stack_interface_1_out_data, not_6_out, and_5_out, IO_DATA_in

  assign IO_DATA_out = IO_DATA_in;

  // Other names for the same wires on the sheet: CMD[1:0] = COMMAND

  // Notes on the sheet:
  //   your circuit must be here
endmodule

module stack_interface (
  input  CLK,
  input  RESET,
  input  [1:0] COMMAND,
  input  [2:0] INDEX,
  input  [3:0] IN_DATA,
  output [3:0] d0,
  output [3:0] d1,
  output [3:0] d2,
  output [3:0] d3,
  output [3:0] d4,
  output [3:0] OUT_DATA
);

  wire parser_1_write_flag;
  wire [2:0] parser_1_ask_index, STACK_POINTER;

  parser parser_1 (
    .CLK(CLK), .COMMAND(COMMAND), .POINTER(STACK_POINTER), .INDEX(INDEX), .WRITE_FLAG(parser_1_write_flag),
    .ASK_INDEX(parser_1_ask_index));
  get_stack_pointer get_stack_pointer_1 (.CLK(CLK), .RESET(RESET), .COMMAND(COMMAND), .CURRENT_POINTER(STACK_POINTER));
  big_memory big_memory_1 (
    .INDEX(parser_1_ask_index), .CLK(parser_1_write_flag), .RESET(RESET), .IN_DATA(IN_DATA),
    .OUT_DATA(OUT_DATA), .d0(d0), .d1(d1), .d2(d2), .d3(d3), .d4(d4));
endmodule

module RS_trigger (
  input  R,
  input  CLK,
  input  S,
  input  RESET,
  output Q,
  output NQ
);

  wire and_1_out, and_2_out, nor_2_out, or_1_out, por_1_out;

  and and_1 (and_1_out, R, CLK);
  and and_2 (and_2_out, CLK, S);
  POR por_1 (.out(por_1_out));
  nor nor_1 (Q, NQ, and_1_out);
  nor nor_2 (nor_2_out, and_2_out, Q);
  or or_1 (or_1_out, RESET, por_1_out);
  or or_2 (NQ, or_1_out, nor_2_out);
endmodule

module D_trigger (
  input  RESET,
  input  D,
  input  CLK,
  output Q,
  output NQ
);

  wire not_1_out;

  not not_1 (not_1_out, D);
  RS_trigger rs_trigger_1 (.R(not_1_out), .CLK(CLK), .S(D), .RESET(RESET), .Q(Q), .NQ(NQ));
endmodule

module memory_cell4 (
  input  RESET,
  input  CLK,
  input  [3:0] IN_DATA,
  output [3:0] OUT_DATA
);

  D_trigger d_trigger_1 (.RESET(RESET), .D(IN_DATA[0]), .CLK(CLK), .Q(OUT_DATA[0]));  // open: NQ
  D_trigger d_trigger_2 (.RESET(RESET), .D(IN_DATA[1]), .CLK(CLK), .Q(OUT_DATA[1]));  // open: NQ
  D_trigger d_trigger_3 (.RESET(RESET), .D(IN_DATA[2]), .CLK(CLK), .Q(OUT_DATA[2]));  // open: NQ
  D_trigger d_trigger_4 (.RESET(RESET), .D(IN_DATA[3]), .CLK(CLK), .Q(OUT_DATA[3]));  // open: NQ
endmodule

module mod_5 (
  input  [2:0] I_DATA,
  output [2:0] O_DATA
);

  wire and_1_out, and_2_out, and_3_out, and_4_out, and_5_out, and_6_out, and_8_out, not_1_out, not_2_out,
       not_3_out;

  not not_1 (not_1_out, I_DATA[0]);
  not not_2 (not_2_out, I_DATA[1]);
  not not_3 (not_3_out, I_DATA[2]);
  and and_1 (and_1_out, I_DATA[0], I_DATA[1]);
  and and_2 (and_2_out, I_DATA[1], I_DATA[2]);
  and and_3 (and_3_out, not_3_out, I_DATA[0]);
  and and_4 (and_4_out, not_3_out, I_DATA[1]);
  and and_5 (and_5_out, not_1_out, not_2_out);
  and and_6 (and_6_out, not_1_out, and_2_out);
  and and_7 (O_DATA[2], and_5_out, I_DATA[2]);
  and and_8 (and_8_out, and_1_out, I_DATA[2]);
  or or_1 (O_DATA[1], and_4_out, and_8_out);
  or or_2 (O_DATA[0], and_3_out, and_6_out);
endmodule

module get_stack_pointer (
  input  CLK,
  input  RESET,
  input  [1:0] COMMAND,
  output [2:0] CURRENT_POINTER
);

  wire and_1_out, and_2_out, d_trigger_1_q, d_trigger_2_q, nand_1_out, not_1_out, not_2_out, not_3_out,
       not_4_out, not_5_out, or_1_out, POP_out, PUSH_out, SHIFT_FLAG;
  wire [2:0] memory_cell3_1_out_data, mod5_calculate_1_o_data;

  not not_1 (not_1_out, COMMAND[0]);
  not not_2 (not_2_out, COMMAND[1]);
  not not_3 (not_3_out, SHIFT_FLAG);
  and POP (POP_out, not_1_out, COMMAND[1]);
  and PUSH (PUSH_out, COMMAND[0], not_2_out);
  memory_cell3 memory_cell3_1 (
    .RESET(RESET), .CLK(not_3_out), .IN_DATA(CURRENT_POINTER), .OUT_DATA(memory_cell3_1_out_data));
  mod5_calculate mod5_calculate_1 (.I_DATA(memory_cell3_1_out_data), .PM(and_1_out), .O_DATA(mod5_calculate_1_o_data));
  D_trigger d_trigger_1 (.RESET(RESET), .D(POP_out), .CLK(CLK), .Q(d_trigger_1_q));  // open: NQ
  D_trigger d_trigger_2 (.RESET(RESET), .D(PUSH_out), .CLK(CLK), .Q(d_trigger_2_q));  // open: NQ
  not not_4 (not_4_out, CLK);
  and and_1 (and_1_out, d_trigger_1_q, not_5_out);
  not not_5 (not_5_out, CLK);
  memory_cell3 memory_cell3_2 (
    .RESET(RESET), .CLK(SHIFT_FLAG), .IN_DATA(mod5_calculate_1_o_data), .OUT_DATA(CURRENT_POINTER));
  and and_2 (and_2_out, d_trigger_2_q, not_4_out);
  nand nand_1 (nand_1_out, d_trigger_2_q, d_trigger_1_q);
  or or_1 (or_1_out, and_2_out, and_1_out);
  and and_3 (SHIFT_FLAG, nand_1_out, or_1_out);

  // Other names for the same wires on the sheet: IS_RESET = RESET
endmodule

module mod5_calculate (
  input  [2:0] I_DATA,
  input  PM,
  output [2:0] O_DATA
);

  wire and_1_out, and_2_out, and_3_out, and_4_out, and_5_out, and_6_out, and_7_out, and_8_out, nand_1_out,
       nor_1_out, nor_2_out, nor_3_out, not_1_out, not_2_out, xnor_1_out, xor_1_out, xor_2_out;
  wire [2:0] mod_5_1_o_data;

  nor nor_1 (nor_1_out, mod_5_1_o_data[0], mod_5_1_o_data[1], mod_5_1_o_data[2]);
  not not_1 (not_1_out, PM);
  mod_5 mod_5_1 (.I_DATA(I_DATA), .O_DATA(mod_5_1_o_data));
  nand nand_1 (nand_1_out, mod_5_1_o_data[0], mod_5_1_o_data[1]);
  nor nor_2 (nor_2_out, nand_1_out, mod_5_1_o_data[2]);
  and and_1 (and_1_out, nor_1_out, PM);
  and and_2 (and_2_out, nor_2_out, not_1_out);
  or or_1 (O_DATA[2], and_1_out, and_2_out);
  xor xor_1 (xor_1_out, mod_5_1_o_data[0], mod_5_1_o_data[1]);
  and and_3 (and_3_out, xor_1_out, not_1_out);
  xor xor_2 (xor_2_out, mod_5_1_o_data[2], mod_5_1_o_data[1]);
  xnor xnor_1 (xnor_1_out, mod_5_1_o_data[1], mod_5_1_o_data[0]);
  and and_4 (and_4_out, xor_2_out, xnor_1_out);
  and and_5 (and_5_out, and_4_out, PM);
  not not_2 (not_2_out, mod_5_1_o_data[0]);
  or or_2 (O_DATA[1], and_3_out, and_5_out);
  and and_6 (and_6_out, xor_2_out, not_2_out);
  nor nor_3 (nor_3_out, mod_5_1_o_data[0], mod_5_1_o_data[2]);
  and and_7 (and_7_out, and_6_out, PM);
  and and_8 (and_8_out, nor_3_out, not_1_out);
  or or_3 (O_DATA[0], and_8_out, and_7_out);
endmodule

module memory_cell3 (
  input  RESET,
  input  CLK,
  input  [2:0] IN_DATA,
  output [2:0] OUT_DATA
);

  D_trigger d_trigger_1 (.RESET(RESET), .D(IN_DATA[0]), .CLK(CLK), .Q(OUT_DATA[0]));  // open: NQ
  D_trigger d_trigger_2 (.RESET(RESET), .D(IN_DATA[1]), .CLK(CLK), .Q(OUT_DATA[1]));  // open: NQ
  D_trigger d_trigger_3 (.RESET(RESET), .D(IN_DATA[2]), .CLK(CLK), .Q(OUT_DATA[2]));  // open: NQ
endmodule

module big_memory (
  input  [2:0] INDEX,
  input  CLK,
  input  RESET,
  input  [3:0] IN_DATA,
  output [3:0] OUT_DATA,
  output [3:0] d0,
  output [3:0] d1,
  output [3:0] d2,
  output [3:0] d3,
  output [3:0] d4
);

  wire NCLK;
  wire [2:0] mod_5_1_o_data;
  wire [4:0] demux_1_out_data;

  not not_1 (NCLK, CLK);
  mod_5 mod_5_1 (.I_DATA(INDEX), .O_DATA(mod_5_1_o_data));
  demux demux_1 (.INDEX(mod_5_1_o_data), .CLK(CLK), .OUT_DATA(demux_1_out_data));
  memory_cell4 memory_cell4_1 (.RESET(RESET), .CLK(demux_1_out_data[0]), .IN_DATA(IN_DATA), .OUT_DATA(d0));
  memory_cell4 memory_cell4_2 (.RESET(RESET), .CLK(demux_1_out_data[1]), .IN_DATA(IN_DATA), .OUT_DATA(d1));
  memory_cell4 memory_cell4_3 (.RESET(RESET), .CLK(demux_1_out_data[2]), .IN_DATA(IN_DATA), .OUT_DATA(d2));
  memory_cell4 memory_cell4_4 (.RESET(RESET), .CLK(demux_1_out_data[3]), .IN_DATA(IN_DATA), .OUT_DATA(d3));
  memory_cell4 memory_cell4_5 (.RESET(RESET), .CLK(demux_1_out_data[4]), .IN_DATA(IN_DATA), .OUT_DATA(d4));
  mux4 mux4_1 (.INDEX(mod_5_1_o_data), .A(d0), .B(d1), .C(d2), .D(d3), .E(d4), .OUT_DATA(OUT_DATA));
endmodule

module demux (
  input  [2:0] INDEX,
  input  CLK,
  output [4:0] OUT_DATA
);

  wire decoder_1_q0, decoder_1_q1, decoder_1_q2, decoder_1_q3, decoder_1_q4;

  decoder decoder_1 (
    .A0(INDEX[0]), .A1(INDEX[1]), .A2(INDEX[2]), .Q0(decoder_1_q0), .Q1(decoder_1_q1), .Q2(decoder_1_q2),
    .Q3(decoder_1_q3), .Q4(decoder_1_q4));
  and and_1 (OUT_DATA[0], decoder_1_q0, CLK);
  and and_2 (OUT_DATA[1], decoder_1_q1, CLK);
  and and_3 (OUT_DATA[2], decoder_1_q2, CLK);
  and and_4 (OUT_DATA[3], decoder_1_q3, CLK);
  and and_5 (OUT_DATA[4], decoder_1_q4, CLK);
endmodule

module mux (
  input  [2:0] INDEX,
  input  IN0,
  input  IN1,
  input  IN2,
  input  IN3,
  input  IN4,
  output OUT_DATA
);

  wire and_1_out, and_2_out, and_3_out, and_4_out, and_5_out, decoder_1_q0, decoder_1_q1, decoder_1_q2,
       decoder_1_q3, decoder_1_q4;

  decoder decoder_1 (
    .A0(INDEX[0]), .A1(INDEX[1]), .A2(INDEX[2]), .Q0(decoder_1_q0), .Q1(decoder_1_q1), .Q2(decoder_1_q2),
    .Q3(decoder_1_q3), .Q4(decoder_1_q4));
  and and_1 (and_1_out, decoder_1_q0, IN0);
  and and_2 (and_2_out, decoder_1_q1, IN1);
  and and_3 (and_3_out, decoder_1_q2, IN2);
  and and_4 (and_4_out, decoder_1_q3, IN3);
  and and_5 (and_5_out, decoder_1_q4, IN4);
  or or_1 (OUT_DATA, and_1_out, and_2_out, and_3_out, and_4_out, and_5_out);
endmodule

module parser (
  input  CLK,
  input  [1:0] COMMAND,
  input  [2:0] POINTER,
  input  [2:0] INDEX,
  output WRITE_FLAG,
  output [2:0] ASK_INDEX
);

  wire and_4_out, and_5_out, GET, not_1_out, not_2_out, or_1_out, POP, PUSH;
  wire [2:0] count_sum_mod5_1_sum, shift_pointer_1_shifted_point, shifter_1_out_data;

  not not_1 (not_1_out, COMMAND[1]);
  not not_2 (not_2_out, COMMAND[0]);
  and and_1 (PUSH, COMMAND[0], not_1_out);
  and and_2 (GET, COMMAND[0], COMMAND[1]);
  and and_3 (POP, not_2_out, COMMAND[1]);
  shifter shifter_1 (.INP_DATA(INDEX), .OUT_DATA(shifter_1_out_data));
  and and_4 (and_4_out, POP, CLK);
  shift_pointer shift_pointer_1 (.COMMAND(COMMAND), .POINTER(POINTER), .SHIFTED_POINT(shift_pointer_1_shifted_point));
  or or_1 (or_1_out, PUSH, and_4_out);
  and and_5 (and_5_out, GET, CLK);
  count_sum_mod5 count_sum_mod5_1 (.X(POINTER), .Y(shifter_1_out_data), .SUM(count_sum_mod5_1_sum));
  and and_6 (WRITE_FLAG, PUSH, CLK);
  select_index select_index_1 (
    .A(or_1_out), .B(and_5_out), .INDEX_A(shift_pointer_1_shifted_point), .INDEX_B(count_sum_mod5_1_sum),
    .ASK_INDEX(ASK_INDEX));
endmodule

module select_index (
  input  A,
  input  B,
  input  [2:0] INDEX_A,
  input  [2:0] INDEX_B,
  output [2:0] ASK_INDEX
);

  wire and_1_out, and_2_out, and_3_out, and_4_out, and_5_out, and_6_out;

  and and_1 (and_1_out, A, INDEX_A[0]);
  and and_2 (and_2_out, A, INDEX_A[1]);
  and and_3 (and_3_out, A, INDEX_A[2]);
  and and_4 (and_4_out, B, INDEX_B[0]);
  and and_5 (and_5_out, B, INDEX_B[1]);
  and and_6 (and_6_out, B, INDEX_B[2]);
  or or_1 (ASK_INDEX[0], and_1_out, and_4_out);
  or or_2 (ASK_INDEX[1], and_2_out, and_5_out);
  or or_3 (ASK_INDEX[2], and_3_out, and_6_out);
endmodule

module count_sum_mod5 (
  input  [2:0] X,
  input  [2:0] Y,
  output [2:0] SUM
);

  wire [2:0] A, B, C, X_t, Y_t;

  or or_1 (SUM[0], A[0], B[0], C[0]);
  mod_5 mod_5_1 (.I_DATA(X), .O_DATA(X_t));
  mod_5 mod_5_2 (.I_DATA(Y), .O_DATA(Y_t));
  or or_2 (SUM[1], A[1], B[1], C[1]);
  count_sum34 count_sum34_1 (.X(X_t), .Y(Y_t), .SUM(A));
  count_sum22 count_sum22_1 (.X(X_t), .Y(Y_t), .SUM(B));
  count_sum0 count_sum0_1 (.X(X_t), .Y(Y_t), .SUM(C));
  or or_3 (SUM[2], A[2], B[2], C[2]);
endmodule

module decoder (
  input  A0,
  input  A1,
  input  A2,
  output Q0,
  output Q1,
  output Q2,
  output Q3,
  output Q4
);

  wire NA0, NA1, NA2;

  not not_1 (NA0, A0);
  not not_2 (NA1, A1);
  not not_3 (NA2, A2);
  and and_1 (Q0, NA0, NA1, NA2);
  and and_2 (Q1, A0, NA1, NA2);
  and and_3 (Q2, NA0, A1, NA2);
  and and_4 (Q3, A0, A1, NA2);
  and and_5 (Q4, NA0, NA1, A2);
endmodule

module mux4 (
  input  [2:0] INDEX,
  input  [3:0] A,
  input  [3:0] B,
  input  [3:0] C,
  input  [3:0] D,
  input  [3:0] E,
  output [3:0] OUT_DATA
);

  mux mux_1 (.INDEX(INDEX), .IN0(A[0]), .IN1(B[0]), .IN2(C[0]), .IN3(D[0]), .IN4(E[0]), .OUT_DATA(OUT_DATA[0]));
  mux mux_2 (.INDEX(INDEX), .IN0(A[1]), .IN1(B[1]), .IN2(C[1]), .IN3(D[1]), .IN4(E[1]), .OUT_DATA(OUT_DATA[1]));
  mux mux_3 (.INDEX(INDEX), .IN0(A[2]), .IN1(B[2]), .IN2(C[2]), .IN3(D[2]), .IN4(E[2]), .OUT_DATA(OUT_DATA[2]));
  mux mux_4 (.INDEX(INDEX), .IN0(A[3]), .IN1(B[3]), .IN2(C[3]), .IN3(D[3]), .IN4(E[3]), .OUT_DATA(OUT_DATA[3]));
endmodule

module count_sum0 (
  input  [2:0] X,
  input  [2:0] Y,
  output [2:0] SUM
);

  wire ZEROX, ZEROY;
  wire [2:0] SUMX, SUMY;

  and and_1 (SUMX[0], X[0], ZEROY);
  and and_2 (SUMX[1], X[1], ZEROY);
  and and_3 (SUMX[2], X[2], ZEROY);
  nor nor_1 (ZEROY, Y[0], Y[1], Y[2]);
  nor nor_2 (ZEROX, X[0], X[1], X[2]);
  or or_1 (SUM[0], SUMX[0], SUMY[0]);
  or or_2 (SUM[1], SUMX[1], SUMY[1]);
  or or_3 (SUM[2], SUMX[2], SUMY[2]);
  and and_4 (SUMY[0], ZEROX, Y[0]);
  and and_5 (SUMY[1], ZEROX, Y[1]);
  and and_6 (SUMY[2], ZEROX, Y[2]);
endmodule

module count_sum22 (
  input  [2:0] X,
  input  [2:0] Y,
  output [2:0] SUM
);

  wire FLAG, less2_1_is_less, less2_2_is_less, not_1_out, not_2_out, or_1_out, or_2_out, or_3_out, xor_1_out,
       xor_2_out;
  wire [1:1] THREE, TWO;
  wire [2:2] FOUR;

  xor xor_1 (xor_1_out, X[0], Y[0]);
  xor xor_2 (xor_2_out, X[1], Y[1]);
  less2 less2_1 (.INP(X), .IS_LESS(less2_1_is_less));
  less2 less2_2 (.INP(Y), .IS_LESS(less2_2_is_less));
  or NEQ (THREE[1], xor_1_out, xor_2_out);
  and and_1 (FLAG, less2_1_is_less, less2_2_is_less);
  not not_1 (not_1_out, THREE[1]);
  not not_2 (not_2_out, THREE[1]);
  and and_2 (TWO[1], not_1_out, X[0]);
  and and_3 (FOUR[2], not_2_out, X[1]);
  and and_4 (SUM[0], FLAG, or_1_out);
  or or_1 (or_1_out, THREE[1], 1'b0, 1'b0);
  or or_2 (or_2_out, THREE[1], TWO[1], 1'b0);
  or or_3 (or_3_out, 1'b0, 1'b0, FOUR[2]);
  and and_5 (SUM[1], FLAG, or_2_out);
  and and_6 (SUM[2], FLAG, or_3_out);

  // Other names for the same wires on the sheet: S0 = SUM[0]; S1 = SUM[1]; S2 = SUM[2]; THREE[0] = THREE[1]
endmodule

module less2 (
  input  [2:0] INP,
  output IS_LESS
);

  wire and_1_out, nor_1_out, or_1_out;

  and and_1 (and_1_out, INP[0], INP[1]);
  nor nor_1 (nor_1_out, and_1_out, INP[2]);
  or or_1 (or_1_out, INP[0], INP[1], INP[2]);
  and and_2 (IS_LESS, nor_1_out, or_1_out);
endmodule

module count_sum34 (
  input  [2:0] X,
  input  [2:0] Y,
  output [2:0] SUM
);

  wire and_6_out, and_8_out, FLAG, less2_1_is_less, less2_2_is_less, nand_1_out, not_1_out, not_2_out,
       not_3_out, not_5_out, or_1_out, or_2_out, or_3_out, or_4_out, or_5_out, S0, S1, S2, xnor_1_out;
  wire [0:0] ONE;
  wire [1:1] THREE, TWO;
  wire [2:2] FOUR;

  not not_1 (not_1_out, S0);
  and and_1 (FOUR[2], not_1_out, S1, not_2_out);
  not not_2 (not_2_out, S2);
  xnor xnor_1 (xnor_1_out, S2, S1);
  not not_3 (not_3_out, S0);
  xor xor_1 (S0, X[0], Y[0]);
  xor xor_2 (S1, X[1], Y[1]);
  xor xor_3 (S2, X[2], Y[2]);
  or or_1 (or_1_out, 1'b0, TWO[1], THREE[1], 1'b0);
  nand nand_1 (nand_1_out, X[2], Y[2]);
  and and_2 (SUM[1], FLAG, or_1_out);
  and and_3 (ONE[0], xnor_1_out, nand_1_out, not_3_out);
  not not_4 (THREE[1], nand_1_out);
  and and_4 (TWO[1], S0, S1, S2);
  or or_2 (or_2_out, 1'b0, 1'b0, 1'b0, FOUR[2]);
  and and_5 (SUM[2], FLAG, or_2_out);
  or or_3 (or_3_out, Y[0], Y[1], Y[2]);
  or or_4 (or_4_out, X[0], X[1], X[2]);
  or or_5 (or_5_out, ONE[0], 1'b0, THREE[1], 1'b0);
  and and_6 (and_6_out, or_4_out, or_3_out);
  less2 less2_1 (.INP(X), .IS_LESS(less2_1_is_less));
  less2 less2_2 (.INP(Y), .IS_LESS(less2_2_is_less));
  and and_7 (SUM[0], FLAG, or_5_out);
  and and_8 (and_8_out, less2_1_is_less, less2_2_is_less);
  not not_5 (not_5_out, and_8_out);
  and and_9 (FLAG, and_6_out, not_5_out);

  // Other names for the same wires on the sheet: THREE[0] = THREE[1]
endmodule

module mutex (
  input  RESET,
  input  CLK,
  input  PUSH,
  output PUSH_FLAG
);

  wire and_1_out, d_trigger_1_q, NCLK;

  and and_1 (and_1_out, CLK, PUSH);
  not not_1 (NCLK, CLK);
  D_trigger d_trigger_1 (.RESET(RESET), .D(and_1_out), .CLK(CLK), .Q(d_trigger_1_q));  // open: NQ
  and and_2 (PUSH_FLAG, NCLK, d_trigger_1_q);
endmodule

module shifter (
  input  [2:0] INP_DATA,
  output [2:0] OUT_DATA
);

  wire [2:1] mod_5_1_o_data;

  mod_5 mod_5_1 (.I_DATA(INP_DATA), .O_DATA({mod_5_1_o_data, OUT_DATA[0]}));
  nor nor_1 (OUT_DATA[2], OUT_DATA[0], mod_5_1_o_data[1], mod_5_1_o_data[2]);
  xor xor_1 (OUT_DATA[1], OUT_DATA[0], mod_5_1_o_data[1]);

  // Other names for the same wires on the sheet: A0 = OUT_DATA[0]; A1 = OUT_DATA[1]; A2 = OUT_DATA[2]
endmodule

module shift_pointer (
  input  [1:0] COMMAND,
  input  [2:0] POINTER,
  output [2:0] SHIFTED_POINT
);

  wire and_4_out, and_5_out, and_6_out, and_7_out, and_8_out, and_9_out, GET, not_1_out, not_2_out, POP, PUSH;
  wire [2:0] mod5_calculate_1_o_data;

  not not_1 (not_1_out, COMMAND[1]);
  not not_2 (not_2_out, COMMAND[0]);
  and and_1 (PUSH, COMMAND[0], not_1_out);
  and and_2 (GET, COMMAND[0], COMMAND[1]);
  and and_3 (POP, not_2_out, COMMAND[1]);
  mod5_calculate mod5_calculate_1 (.I_DATA(POINTER), .PM(1'b1), .O_DATA(mod5_calculate_1_o_data));
  and and_4 (and_4_out, mod5_calculate_1_o_data[0], POP);
  and and_5 (and_5_out, mod5_calculate_1_o_data[1], POP);
  and and_6 (and_6_out, mod5_calculate_1_o_data[2], POP);
  and and_7 (and_7_out, POINTER[0], PUSH);
  and and_8 (and_8_out, POINTER[1], PUSH);
  and and_9 (and_9_out, POINTER[2], PUSH);
  or or_1 (SHIFTED_POINT[0], and_4_out, and_7_out);
  or or_2 (SHIFTED_POINT[1], and_5_out, and_8_out);
  or or_3 (SHIFTED_POINT[2], and_9_out, and_6_out);
endmodule
